// Logisim project Zadanie nr 0.circ as structural Verilog: 1 circuit, main circuit main
module main (
  input  a,
  input  b,
  input  c,
  output out_4,
  output out_5,
  output out_6
);

  wire and_1_out, and_2_out, and_3_out, and_4_out, and_5_out, and_6_out, and_7_out, and_8_out, not_1_out,
       not_2_out, or_1_out;

  not not_1 (not_1_out, a);
  not not_2 (not_2_out, b);
  and and_1 (and_1_out, not_1_out, b);
  and and_2 (and_2_out, a, not_2_out);
  and and_3 (and_3_out, a, c);
  and and_4 (and_4_out, a, b);
  and and_5 (and_5_out, b, c);
  and and_6 (and_6_out, b, c);
  and and_7 (and_7_out, a, b);
  or or_1 (or_1_out, c, a);
  or or_2 (out_4, and_1_out, and_2_out);
  or or_3 (out_5, and_3_out, and_5_out);
  // OR_Gate or_4 is placed but not wired
  or or_5 (out_6, and_6_out, and_7_out);
  and and_8 (and_8_out, or_1_out, b);

  // Notes on the sheet:
  //   Zadanie nr 0 (nieoptymalizowane)
  //   Zadanie nr 0 (optymalizowane)
  //   XOR circuit
endmodule
