// Logisim project lab1.1-ex.circ as structural Verilog: 1 circuit, main circuit main
module main (
);

  wire and_1_out, and_2_out, and_3_out, button_1_out, d_ff_1_q, d_ff_1_qn, d_ff_2_q, d_ff_2_qn, d_ff_3_qn,
       dip_7400_1_p5, dip_7400_1_p6, dip_7400_1_p8, dip_7400_1_p11, dip_7400_1_p12, dip_7400_2_p5,
       dip_7400_2_p6, dip_7400_2_p11, dip_7400_2_p12, dip_7400_3_p3, dip_7400_3_p6, nand_1_out, nand_2_out,
       nand_3_out, nand_4_out, nand_5_out, nand_6_out, nand_7_out, nand_8_out, nand_9_out, nand_10_out,
       nand_11_out, nand_12_out, nand_13_out, nand_14_out, nand_15_out, nand_16_out, nand_17_out,
       nand_18_out, nand_19_out, nand_20_out, nand_21_out, nand_22_out, nand_23_out, nand_24_out, not_1_out,
       not_2_out;

  Button button_1 (.out(button_1_out));
  D_Flip_Flop d_ff_1 (.D(d_ff_1_qn), .clk(button_1_out), .Q(d_ff_1_q), .Qn(d_ff_1_qn));  // open: preset, reset
  D_Flip_Flop d_ff_2 (.D(d_ff_2_qn), .clk(d_ff_1_q), .Q(d_ff_2_q), .Qn(d_ff_2_qn));  // open: preset, reset
  not not_1 (not_1_out, d_ff_2_q);
  not not_2 (not_2_out, dip_7400_1_p8);
  // DIP_7400 dip_7400_1: pin names not known; wires that end beside it: d_ff_1_q, d_ff_2_q, d_ff_2_q, d_ff_2_q, dip_7400_1_p5, dip_7400_1_p6, d_ff_2_q, dip_7400_1_p8, dip_7400_1_p8, dip_7400_1_p8, dip_7400_1_p11, dip_7400_1_p12
  and and_1 (and_1_out, d_ff_1_q, d_ff_2_q);
  and and_2 (and_2_out, d_ff_2_q, dip_7400_1_p8);
  and and_3 (and_3_out, d_ff_1_q, not_2_out);
  nand nand_1 (nand_1_out, d_ff_1_q, d_ff_2_q);
  nand nand_2 (nand_2_out, d_ff_2_q, dip_7400_1_p8);
  nand nand_3 (nand_3_out, d_ff_2_q, d_ff_2_q);
  nand nand_4 (nand_4_out, dip_7400_1_p8, dip_7400_1_p8);
  nand nand_5 (nand_5_out, d_ff_1_q, d_ff_2_q);
  nand nand_6 (nand_6_out, d_ff_2_q, dip_7400_1_p8);
  nand nand_7 (nand_7_out, d_ff_2_q, d_ff_2_q);
  nand nand_8 (nand_8_out, dip_7400_1_p8, dip_7400_1_p8);
  D_Flip_Flop d_ff_3 (.D(d_ff_3_qn), .clk(d_ff_2_q), .Q(dip_7400_1_p8), .Qn(d_ff_3_qn));  // open: preset, reset
  // OR_Gate or_1 has open pins: in0=and_1_out, in1=and_2_out, in2=and_3_out, out=open
  nand nand_9 (nand_9_out, nand_3_out, nand_4_out);
  nand nand_10 (nand_10_out, nand_5_out, nand_5_out);
  nand nand_11 (nand_11_out, nand_6_out, nand_6_out);
  nand nand_12 (nand_12_out, nand_7_out, nand_8_out);
  // DIP_7400 dip_7400_2: pin names not known; wires that end beside it: dip_7400_1_p11, dip_7400_1_p12, dip_7400_1_p5, dip_7400_1_p6, dip_7400_2_p5, dip_7400_2_p6, dip_7400_2_p5, dip_7400_2_p6, dip_7400_2_p5, dip_7400_2_p6, dip_7400_2_p11, dip_7400_2_p12
  nand nand_13 (nand_13_out, nand_9_out, nand_9_out);
  nand nand_14 (nand_14_out, nand_12_out, nand_12_out);
  nand nand_15 (nand_15_out, d_ff_1_q, nand_13_out);
  nand nand_16 (nand_16_out, nand_10_out, nand_10_out);
  nand nand_17 (nand_17_out, nand_11_out, nand_11_out);
  nand nand_18 (nand_18_out, d_ff_1_q, nand_14_out);
  // DIP_7400 dip_7400_3: pin names not known; wires that end beside it: dip_7400_2_p11, d_ff_1_q, dip_7400_3_p3, dip_7400_3_p3, dip_7400_2_p12, dip_7400_3_p6
  nand nand_19 (nand_19_out, nand_1_out, nand_2_out);
  nand nand_20 (nand_20_out, nand_16_out, nand_17_out);
  LED led_1 (.in(dip_7400_3_p6));
  nand nand_21 (nand_21_out, nand_19_out, nand_19_out);
  nand nand_22 (nand_22_out, nand_20_out, nand_20_out);
  nand nand_23 (nand_23_out, nand_21_out, nand_15_out);
  LED led_2 (.in(nand_23_out));
  nand nand_24 (nand_24_out, nand_22_out, nand_18_out);
  LED led_3 (.in(nand_24_out));

  // Notes on the sheet:
  //   b
  //   a
  //   c
  //   Optymalizacja tego niżej
endmodule
