// Logisim project lab1_b.circ as structural Verilog: 1 circuit, main circuit main
module main (
  input  in_1
);

  wire and_1_out, and_2_out, and_3_out, and_4_out, and_5_out, and_6_out, and_7_out, and_8_out, and_9_out,
       and_10_out, and_11_out, and_12_out, and_13_out, clock_1_out, n7410_1_pin8, n7410_1_pin9, nor_1_out,
       nor_2_out, nor_3_out, nor_4_out, nor_5_out, nor_6_out, not_1_out, not_2_out, not_3_out, not_4_out,
       not_5_out, not_6_out, not_7_out, s_r_ff_1_q, s_r_ff_2_q, s_r_ff_3_q, undriven, undriven_2, undriven_3,
       undriven_4, undriven_5;

  not not_1 (not_1_out, 1'b0);
  not not_2 (not_2_out, in_1);
  Clock clock_1 (.out(clock_1_out));
  nor nor_1 (nor_1_out, not_1_out, not_2_out);
  and and_1 (and_1_out, not_2_out, not_1_out);
  not not_3 (not_3_out, in_1);
  and and_2 (and_2_out, undriven, not_2_out);
  nor nor_2 (nor_2_out, and_1_out, clock_1_out);
  and and_3 (and_3_out, nor_1_out, undriven_2);
  and and_4 (and_4_out, not_1_out, s_r_ff_2_q);
  nor nor_3 (nor_3_out, and_2_out, and_3_out, and_4_out);
  S_R_Flip_Flop s_r_ff_1 (
    .S(not_4_out), .R(nor_3_out), .clk(nor_2_out), .Q(s_r_ff_1_q), .reset(not_3_out));  // open: Qn, preset
  not not_4 (not_4_out, nor_3_out);
  and and_5 (and_5_out, s_r_ff_1_q, not_2_out);
  and and_6 (and_6_out, nor_1_out, undriven_3);
  nor nor_4 (nor_4_out, and_5_out, and_6_out, and_7_out);
  LED led_1 (.in(s_r_ff_1_q));
  and and_7 (and_7_out, not_1_out, s_r_ff_3_q);
  S_R_Flip_Flop s_r_ff_2 (
    .S(not_5_out), .R(nor_4_out), .clk(nor_2_out), .Q(s_r_ff_2_q), .reset(not_3_out));  // open: Qn, preset
  not not_5 (not_5_out, nor_4_out);
  and and_8 (and_8_out, s_r_ff_2_q, not_2_out);
  LED led_2 (.in(s_r_ff_2_q));
  and and_9 (and_9_out, nor_1_out, undriven_4);
  nor nor_5 (nor_5_out, and_8_out, and_9_out, and_10_out);
  and and_10 (and_10_out, not_1_out, n7410_1_pin9);
  S_R_Flip_Flop s_r_ff_3 (
    .S(not_6_out), .R(nor_5_out), .clk(nor_2_out), .Q(s_r_ff_3_q), .reset(not_3_out));  // open: Qn, preset
  not not_6 (not_6_out, nor_5_out);
  _7410 #(.ShowInternalStructure("true")) u_7410_1 (
    .pin11(s_r_ff_2_q), .pin10(s_r_ff_3_q), .pin9(n7410_1_pin9), .pin8(n7410_1_pin8));  // open: pin1, pin2, pin3, pin4, pin5, pin6, pin13, pin12
  and and_11 (and_11_out, s_r_ff_3_q, not_2_out);
  LED led_3 (.in(s_r_ff_3_q));
  and and_12 (and_12_out, nor_1_out, undriven_5);
  nor nor_6 (nor_6_out, and_11_out, and_12_out, and_13_out);
  not not_7 (not_7_out, nor_6_out);
  and and_13 (and_13_out, not_1_out, n7410_1_pin8);
  S_R_Flip_Flop s_r_ff_4 (
    .S(not_7_out), .R(nor_6_out), .clk(nor_2_out), .Q(n7410_1_pin9), .reset(not_3_out));  // open: Qn, preset
  LED led_4 (.in(n7410_1_pin9));

  // Notes on the sheet:
  //   S0
  //   Mode control
  //   S1
  //   Clock
  //   Clear
  //   Shift Right Serial Input
  //   A
  //   B
  //   C
  //   D
  //   Shift Left Serial Input
endmodule
