// Logisim project lab1_c.circ as structural Verilog: 1 circuit, main circuit main
module main (
  input  S1
);

  wire and_1_out, and_2_out, and_3_out, and_4_out, and_5_out, and_6_out, and_7_out, and_8_out, and_9_out,
       and_10_out, and_11_out, and_12_out, and_13_out, clock_1_out, n7404_1_pin2, nor_1_out, nor_2_out,
       nor_3_out, nor_4_out, nor_5_out, nor_6_out, not_1_out, not_2_out, not_3_out, not_4_out, not_5_out,
       not_6_out, not_7_out, s_r_ff_1_q, s_r_ff_2_q, s_r_ff_3_q, s_r_ff_4_q, undriven, undriven_2,
       undriven_3, undriven_4, undriven_5, undriven_6;

  Clock clock_1 (.out(clock_1_out));
  not not_1 (not_1_out, 1'b0);
  not not_2 (not_2_out, S1);
  nor nor_1 (nor_1_out, not_1_out, not_2_out);
  and and_1 (and_1_out, not_2_out, not_1_out);
  nor nor_2 (nor_2_out, and_1_out, clock_1_out);
  not not_3 (not_3_out, undriven);
  and and_2 (and_2_out, undriven_2, not_2_out);
  and and_3 (and_3_out, nor_1_out, undriven_3);
  nor nor_3 (nor_3_out, and_2_out, and_3_out, and_4_out);
  and and_4 (and_4_out, not_1_out, s_r_ff_2_q);
  S_R_Flip_Flop s_r_ff_1 (
    .S(not_4_out), .R(nor_3_out), .clk(nor_2_out), .Q(s_r_ff_1_q), .reset(not_3_out));  // open: Qn, preset
  not not_4 (not_4_out, nor_3_out);
  and and_5 (and_5_out, s_r_ff_1_q, not_2_out);
  LED led_1 (.in(s_r_ff_1_q));
  and and_6 (and_6_out, nor_1_out, undriven_4);
  nor nor_4 (nor_4_out, and_5_out, and_6_out, and_7_out);
  _7404 #(.ShowInternalStructure("true")) u_7404_1 (
    .pin1(s_r_ff_1_q), .pin2(n7404_1_pin2));  // open: pin3, pin4, pin5, pin6, pin13, pin12, pin11, pin10, pin9, pin8
  and and_7 (and_7_out, not_1_out, s_r_ff_3_q);
  S_R_Flip_Flop s_r_ff_2 (
    .S(not_5_out), .R(nor_4_out), .clk(nor_2_out), .Q(s_r_ff_2_q), .reset(not_3_out));  // open: Qn, preset
  not not_5 (not_5_out, nor_4_out);
  and and_8 (and_8_out, s_r_ff_2_q, not_2_out);
  LED led_2 (.in(s_r_ff_2_q));
  and and_9 (and_9_out, nor_1_out, undriven_5);
  nor nor_5 (nor_5_out, and_8_out, and_9_out, and_10_out);
  and and_10 (and_10_out, not_1_out, s_r_ff_4_q);
  S_R_Flip_Flop s_r_ff_3 (
    .S(not_6_out), .R(nor_5_out), .clk(nor_2_out), .Q(s_r_ff_3_q), .reset(not_3_out));  // open: Qn, preset
  not not_6 (not_6_out, nor_5_out);
  and and_11 (and_11_out, s_r_ff_3_q, not_2_out);
  LED led_3 (.in(s_r_ff_3_q));
  and and_12 (and_12_out, nor_1_out, undriven_6);
  and and_13 (and_13_out, not_1_out, n7404_1_pin2);
  nor nor_6 (nor_6_out, and_11_out, and_12_out, and_13_out);
  not not_7 (not_7_out, nor_6_out);
  S_R_Flip_Flop s_r_ff_4 (
    .S(not_7_out), .R(nor_6_out), .clk(nor_2_out), .Q(s_r_ff_4_q), .reset(not_3_out));  // open: Qn, preset
  LED led_4 (.in(s_r_ff_4_q));

  // Notes on the sheet:
  //   Mode control
  //   S0
  //   Clock
  //   Clear
  //   Shift Right Serial Input
  //   A
  //   B
  //   C
  //   D
  //   Shift Left Serial Input
endmodule
