// Logisim project lab2function1.circ as structural Verilog: 2 circuits, main circuit main
module main (
  input  a,
  input  b,
  input  c,
  input  d,
  input  in_5
);

  wire and_1_out, and_2_out, m_74151_1_y, nand_1_out, nand_2_out, nand_3_out, nand_4_out, nand_5_out,
       nand_6_out, nand_7_out, nand_8_out, nand_9_out, nand_10_out, nand_11_out, nand_12_out, nand_13_out,
       nand_14_out, nand_15_out, nand_16_out, nand_17_out, nand_18_out, not_1_out, not_2_out, not_3_out,
       not_4_out, not_5_out, not_6_out, not_7_out, not_8_out, not_9_out, not_10_out, or_1_out, or_2_out,
       or_3_out, or_4_out, xnor_1_out;

  not not_1 (not_1_out, a);
  not not_2 (not_2_out, b);
  not not_3 (not_3_out, d);
  not not_4 (not_4_out, c);
  not not_5 (not_5_out, d);
  not not_6 (not_6_out, a);
  and and_1 (and_1_out, not_1_out, not_2_out, not_3_out);
  and and_2 (and_2_out, not_4_out, not_5_out);
  nand nand_1 (nand_1_out, a, a);
  nand nand_2 (nand_2_out, b, b);
  nand nand_3 (nand_3_out, d, d);
  nand nand_4 (nand_4_out, c, c);
  nand nand_5 (nand_5_out, d, d);
  nand nand_6 (nand_6_out, a, a);
  nand nand_7 (nand_7_out, b, b);
  nand nand_8 (nand_8_out, d, d);
  nand nand_9 (nand_9_out, c, c);
  nand nand_10 (nand_10_out, d, d);
  or or_1 (or_1_out, a, b);
  not not_7 (not_7_out, c);
  or or_2 (or_2_out, and_1_out, and_2_out);
  nand nand_11 (nand_11_out, nand_1_out, nand_2_out, nand_3_out);
  nand nand_12 (nand_12_out, nand_4_out, nand_5_out);
  nand nand_13 (nand_13_out, nand_7_out, nand_8_out);
  nand nand_14 (nand_14_out, nand_9_out, nand_10_out);
  not not_8 (not_8_out, or_1_out);
  LED led_1 (.in(or_2_out));
  nand nand_15 (nand_15_out, nand_11_out, nand_12_out);
  nand nand_16 (nand_16_out, nand_13_out, nand_13_out);
  or or_3 (or_3_out, not_8_out, not_7_out);
  not not_9 (not_9_out, or_3_out);
  LED led_2 (.in(nand_15_out));
  nand nand_17 (nand_17_out, nand_6_out, nand_16_out);
  or or_4 (or_4_out, not_9_out, d);
  nand nand_18 (nand_18_out, nand_17_out, nand_14_out);
  LED led_3 (.in(nand_18_out));
  LED led_4 (.in(m_74151_1_y));
  M_74151 m_74151_1 (
    .A(1'b1), .B(1'b0), .C(not_6_out), .D(1'b0), .E(1'b1), .F(1'b0), .G(1'b0), .J(1'b0), .S0(d), .S1(c),
    .S2(b), .OE(in_5), .Y(m_74151_1_y));  // open: Z
  not not_10 (not_10_out, or_4_out);
  NotExactlyOne xnor_1 (
    .out(xnor_1_out), .in0(or_2_out), .in1(nand_15_out), .in2(not_10_out), .in3(nand_18_out),
    .in4(m_74151_1_y));
  LED led_5 (.in(xnor_1_out));

  // Notes on the sheet:
  //   3-inputs-NAND form
  //   AND / OR form
  //   2-inputs-NAND form
  //   OR / NOT form
endmodule

module M_74151 (
  input  A,
  input  B,
  input  C,
  input  D,
  input  E,
  input  F,
  input  G,
  input  J,
  input  S0,
  input  S1,
  input  S2,
  input  OE,
  output Y,
  output Z
);

  wire and_1_out, and_2_out, and_3_out, and_4_out, and_5_out, and_6_out, and_7_out, and_8_out, not_1_out,
       not_2_out, not_3_out, not_4_out;

  not not_1 (not_1_out, S0);
  not not_2 (not_2_out, S1);
  not not_3 (not_3_out, OE);
  not not_4 (not_4_out, S2);
  and and_1 (and_1_out, A, not_3_out, not_1_out, not_2_out, not_4_out);
  and and_2 (and_2_out, B, not_3_out, S0, not_2_out, not_4_out);
  and and_3 (and_3_out, C, not_3_out, not_1_out, S1, not_4_out);
  and and_4 (and_4_out, D, not_3_out, S0, S1, not_4_out);
  and and_5 (and_5_out, E, not_3_out, not_1_out, not_2_out, S2);
  and and_6 (and_6_out, F, not_3_out, S0, not_2_out, S2);
  and and_7 (and_7_out, G, not_3_out, not_1_out, S1, S2);
  and and_8 (and_8_out, J, not_3_out, S0, S1, S2);
  or or_1 (Y, and_1_out, and_2_out, and_3_out, and_4_out, and_5_out, and_6_out, and_7_out, and_8_out);
  not not_5 (Z, Y);
endmodule
