// Logisim project lab4.circ as structural Verilog: 1 circuit, main circuit main
module main (
  input  in_1,
  input  in_2,
  input  in_3
);

  wire and_1_out, and_2_out, and_3_out, and_4_out, clock_1_out, clock_2_out, clock_3_out, d_ff_1_q,
       d_ff_1_qn, d_ff_2_q, d_ff_3_q, d_ff_3_qn, d_ff_4_q, d_ff_5_q, d_ff_5_qn, d_ff_6_q, nand_1_out,
       nand_2_out, nand_3_out, nand_4_out, nand_5_out, nand_6_out, nand_7_out, nand_8_out, nand_9_out,
       nand_10_out, nand_11_out, nand_12_out, nand_13_out, nand_14_out, nand_15_out, nand_16_out,
       nand_17_out, nand_18_out, nand_19_out, nand_20_out, or_1_out, or_2_out;

  and and_1 (and_1_out, d_ff_1_qn, in_1);
  and and_2 (and_2_out, in_1, d_ff_2_q);
  and and_3 (and_3_out, in_1, d_ff_1_q);
  nand nand_1 (nand_1_out, d_ff_3_qn, in_2);
  nand nand_2 (nand_2_out, in_2, d_ff_4_q);
  nand nand_3 (nand_3_out, in_2, d_ff_3_q);
  nand nand_4 (nand_4_out, d_ff_5_qn, in_3);
  nand nand_5 (nand_5_out, in_3, d_ff_6_q);
  nand nand_6 (nand_6_out, in_3, d_ff_5_q);
  D_Flip_Flop d_ff_1 (.D(or_1_out), .clk(clock_1_out), .Q(d_ff_1_q), .Qn(d_ff_1_qn));  // open: preset, reset
  or or_1 (or_1_out, and_1_out, and_2_out);
  or or_2 (or_2_out, and_2_out, and_3_out);
  nand nand_7 (nand_7_out, nand_1_out, nand_1_out);
  nand nand_8 (nand_8_out, nand_2_out, nand_2_out);
  nand nand_9 (nand_9_out, nand_8_out, nand_8_out);
  nand nand_10 (nand_10_out, nand_3_out, nand_3_out);
  nand nand_11 (nand_11_out, nand_10_out, nand_10_out);
  D_Flip_Flop d_ff_2 (.D(or_2_out), .clk(clock_1_out), .Q(d_ff_2_q));  // open: Qn, preset, reset
  Clock clock_1 (.out(clock_1_out));
  nand nand_12 (nand_12_out, nand_7_out, nand_7_out);
  nand nand_13 (nand_13_out, nand_9_out, nand_11_out);
  D_Flip_Flop d_ff_3 (.D(nand_14_out), .clk(clock_2_out), .Q(d_ff_3_q), .Qn(d_ff_3_qn));  // open: preset, reset
  nand nand_14 (nand_14_out, nand_12_out, nand_9_out);
  D_Flip_Flop d_ff_4 (.D(nand_13_out), .clk(clock_2_out), .Q(d_ff_4_q));  // open: Qn, preset, reset
  Clock clock_2 (.out(clock_2_out));
  D_Flip_Flop d_ff_5 (.D(nand_15_out), .clk(clock_3_out), .Q(d_ff_5_q), .Qn(d_ff_5_qn));  // open: preset, reset
  nand nand_15 (nand_15_out, nand_4_out, nand_5_out);
  D_Flip_Flop d_ff_6 (.D(nand_16_out), .clk(clock_3_out), .Q(d_ff_6_q));  // open: Qn, preset, reset
  nand nand_16 (nand_16_out, nand_5_out, nand_6_out);
  Clock clock_3 (.out(clock_3_out));
  and and_4 (and_4_out, d_ff_1_q, d_ff_2_q);
  LED led_1 (.in(and_4_out));
  nand nand_17 (nand_17_out, d_ff_3_q, d_ff_4_q);
  nand nand_18 (nand_18_out, nand_17_out, nand_17_out);
  nand nand_19 (nand_19_out, d_ff_5_q, d_ff_6_q);
  LED led_2 (.in(nand_18_out));
  nand nand_20 (nand_20_out, nand_19_out, nand_19_out);
  LED led_3 (.in(nand_20_out));

  // Notes on the sheet:
  //   Układ podstawowy
  //   NAND z NOT
  //   Optymalny NAND
endmodule
