// Logisim project lab4-mealy.circ as structural Verilog: 1 circuit, main circuit main
module main (
  input  in_1
);

  wire and_1_out, and_2_out, clock_1_out, d_ff_1_q, d_ff_1_qn, xor_1_out;

  D_Flip_Flop d_ff_1 (.D(xor_1_out), .clk(clock_1_out), .Q(d_ff_1_q), .Qn(d_ff_1_qn));  // open: preset, reset
  xor xor_1 (xor_1_out, d_ff_1_q, in_1);
  Clock clock_1 (.out(clock_1_out));
  and and_1 (and_1_out, in_1, d_ff_1_q);
  LED led_1 (.in(and_1_out));
  and and_2 (and_2_out, d_ff_1_qn, in_1);
  LED led_2 (.in(and_2_out));

  // Notes on the sheet:
  //   wejscie x
  //   zegar
  //   z2
  //   z1
endmodule
