// Logisim project lab4-moore.circ as structural Verilog: 1 circuit, main circuit main
module main (
  input  x,
  input  x_2,
  input  x_3
);

  wire and_1_out, and_2_out, and_3_out, and_4_out, and_5_out, and_6_out, clock_1_out, clock_2_out,
       clock_3_out, d_ff_1_q, d_ff_1_qn, d_ff_2_q, d_ff_2_qn, d_ff_3_q, d_ff_3_qn, d_ff_4_q, d_ff_4_qn,
       d_ff_5_q, d_ff_5_qn, d_ff_6_q, d_ff_6_qn, nand_1_out, nand_2_out, nand_3_out, nor_1_out, nor_2_out,
       not_1_out, not_2_out, or_1_out, xor_1_out;

  Clock clock_1 (.out(clock_1_out));
  Clock clock_2 (.out(clock_2_out));
  Clock clock_3 (.out(clock_3_out));
  not not_1 (not_1_out, x);
  not not_2 (not_2_out, x_2);
  and and_1 (and_1_out, d_ff_1_q, not_1_out);
  and and_2 (and_2_out, x, d_ff_1_qn);
  nand nand_1 (nand_1_out, d_ff_2_q, not_2_out);
  nand nand_2 (nand_2_out, x_2, d_ff_2_qn);
  or or_1 (or_1_out, and_1_out, and_2_out);
  nand nand_3 (nand_3_out, nand_1_out, nand_2_out);
  xor xor_1 (xor_1_out, d_ff_3_q, x_3);
  D_Flip_Flop d_ff_1 (.D(or_1_out), .clk(clock_1_out), .Q(d_ff_1_q), .Qn(d_ff_1_qn));  // open: preset, reset
  D_Flip_Flop d_ff_2 (.D(nand_3_out), .clk(clock_2_out), .Q(d_ff_2_q), .Qn(d_ff_2_qn));  // open: preset, reset
  D_Flip_Flop d_ff_3 (.D(xor_1_out), .clk(clock_3_out), .Q(d_ff_3_q), .Qn(d_ff_3_qn));  // open: preset, reset
  D_Flip_Flop d_ff_4 (.D(d_ff_1_q), .clk(clock_1_out), .Q(d_ff_4_q), .Qn(d_ff_4_qn));  // open: preset, reset
  D_Flip_Flop d_ff_5 (.D(d_ff_2_q), .clk(clock_2_out), .Q(d_ff_5_q), .Qn(d_ff_5_qn));  // open: preset, reset
  D_Flip_Flop d_ff_6 (.D(d_ff_3_q), .clk(clock_3_out), .Q(d_ff_6_q), .Qn(d_ff_6_qn));  // open: preset, reset
  and and_3 (and_3_out, d_ff_1_q, d_ff_4_qn);
  and and_4 (and_4_out, d_ff_1_qn, d_ff_4_q);
  nor nor_1 (nor_1_out, d_ff_2_qn, d_ff_5_q);
  nor nor_2 (nor_2_out, d_ff_2_q, d_ff_5_qn);
  and and_5 (and_5_out, d_ff_3_q, d_ff_6_qn);
  and and_6 (and_6_out, d_ff_3_qn, d_ff_6_q);
  LED led_1 (.in(and_3_out));
  LED led_2 (.in(and_4_out));
  LED led_3 (.in(nor_1_out));
  LED led_4 (.in(nor_2_out));
  LED led_5 (.in(and_5_out));
  LED led_6 (.in(and_6_out));

  // Notes on the sheet:
  //   Z1
  //   Z2
  //   Z1
  //   Z2
  //   Z1
  //   Z2
endmodule
